// Logisim project PRACTICA_2.circ as structural Verilog: 9 circuits, main circuit main
module main (
  input  A,
  input  B,
  input  C,
  input  D
);

  wire modulo_7_seg_1_seg_a, modulo_7_seg_1_seg_b, modulo_7_seg_1_seg_c, modulo_7_seg_1_seg_d,
       modulo_7_seg_1_seg_e, modulo_7_seg_1_seg_f, modulo_7_seg_1_seg_g;

  modulo_7_seg modulo_7_seg_1 (
    .A(A), .B(B), .C(C), .D(D), .seg_a(modulo_7_seg_1_seg_a), .seg_b(modulo_7_seg_1_seg_b),
    .seg_c(modulo_7_seg_1_seg_c), .seg_d(modulo_7_seg_1_seg_d), .seg_e(modulo_7_seg_1_seg_e),
    .seg_f(modulo_7_seg_1_seg_f), .seg_g(modulo_7_seg_1_seg_g));
  _7_Segment_Display u_7_segment_display_1 (
    .g(modulo_7_seg_1_seg_g), .f(modulo_7_seg_1_seg_f), .a(modulo_7_seg_1_seg_a), .b(modulo_7_seg_1_seg_b),
    .e(modulo_7_seg_1_seg_e), .d(modulo_7_seg_1_seg_d), .c(modulo_7_seg_1_seg_c));  // open: dp
endmodule

module segmento_a (
  input  A,
  input  B,
  input  C,
  input  D,
  output sa
);

  wire and_1_out, and_2_out, not_1_out, not_2_out, or_1_out, or_2_out;

  not not_1 (not_1_out, B);
  not not_2 (not_2_out, D);
  and and_1 (and_1_out, B, D);
  and and_2 (and_2_out, not_1_out, not_2_out);
  or or_1 (or_1_out, A, and_1_out);
  or or_2 (or_2_out, C, and_2_out);
  or or_3 (sa, or_1_out, or_2_out);
endmodule

module segmento_b (
  input  A,
  input  B,
  input  C,
  input  D,
  output sb
);

  wire and_1_out, and_2_out, not_1_out, not_2_out, not_3_out, or_1_out;

  not not_1 (not_1_out, B);
  not not_2 (not_2_out, C);
  not not_3 (not_3_out, D);
  and and_1 (and_1_out, C, D);
  and and_2 (and_2_out, not_2_out, not_3_out);
  or or_1 (or_1_out, and_1_out, and_2_out);
  or or_2 (sb, not_1_out, or_1_out);
endmodule

module segmento_c (
  input  A,
  input  B,
  input  C,
  input  D,
  output sc
);

  wire not_1_out, or_1_out;

  not not_1 (not_1_out, C);
  or or_1 (or_1_out, B, D);
  or or_2 (sc, not_1_out, or_1_out);
endmodule

module segmento_d (
  input  A,
  input  B,
  input  C,
  input  D,
  output sd
);

  wire and_1_out, and_2_out, and_3_out, and_4_out, and_5_out, not_1_out, not_2_out, not_3_out, or_1_out,
       or_2_out, or_3_out;

  not not_1 (not_1_out, B);
  not not_2 (not_2_out, C);
  and and_1 (and_1_out, not_1_out, C);
  and and_2 (and_2_out, B, not_2_out);
  not not_3 (not_3_out, D);
  and and_3 (and_3_out, and_2_out, D);
  and and_4 (and_4_out, not_1_out, not_3_out);
  or or_1 (or_1_out, A, and_1_out);
  or or_2 (or_2_out, and_3_out, and_4_out);
  and and_5 (and_5_out, C, not_3_out);
  or or_3 (or_3_out, or_1_out, or_2_out);
  or or_4 (sd, or_3_out, and_5_out);
endmodule

module segmento_e (
  input  A,
  input  B,
  input  C,
  input  D,
  output e
);

  wire and_1_out, and_2_out, not_1_out, not_2_out;

  not not_1 (not_1_out, B);
  not not_2 (not_2_out, D);
  and and_1 (and_1_out, not_1_out, not_2_out);
  and and_2 (and_2_out, C, not_2_out);
  or or_1 (e, and_1_out, and_2_out);
endmodule

module segmento_f (
  input  A,
  input  B,
  input  C,
  input  D,
  output f
);

  wire and_1_out, and_2_out, and_3_out, not_1_out, not_2_out, or_1_out, or_2_out;

  not not_1 (not_1_out, C);
  not not_2 (not_2_out, D);
  and and_1 (and_1_out, not_1_out, not_2_out);
  and and_2 (and_2_out, B, not_1_out);
  and and_3 (and_3_out, B, not_2_out);
  or or_1 (or_1_out, and_1_out, and_2_out);
  or or_2 (or_2_out, and_3_out, A);
  or or_3 (f, or_1_out, or_2_out);
endmodule

module segmento_g (
  input  A,
  input  B,
  input  C,
  input  D,
  output g
);

  wire and_1_out, and_2_out, and_3_out, not_1_out, not_2_out, not_3_out, or_1_out, or_2_out;

  not not_1 (not_1_out, B);
  not not_2 (not_2_out, C);
  not not_3 (not_3_out, D);
  and and_1 (and_1_out, not_1_out, C);
  and and_2 (and_2_out, B, not_2_out);
  and and_3 (and_3_out, C, not_3_out);
  or or_1 (or_1_out, and_1_out, and_2_out);
  or or_2 (or_2_out, A, and_3_out);
  or or_3 (g, or_1_out, or_2_out);
endmodule

module modulo_7_seg (
  input  A,
  input  B,
  input  C,
  input  D,
  output seg_a,
  output seg_b,
  output seg_c,
  output seg_d,
  output seg_e,
  output seg_f,
  output seg_g
);

  segmento_a segmento_a_1 (.A(A), .B(B), .C(C), .D(D), .sa(seg_a));
  segmento_b segmento_b_1 (.A(A), .B(B), .C(C), .D(D), .sb(seg_b));
  segmento_c segmento_c_1 (.A(A), .B(B), .C(C), .D(D), .sc(seg_c));
  segmento_d segmento_d_1 (.A(A), .B(B), .C(C), .D(D), .sd(seg_d));
  segmento_e segmento_e_1 (.A(A), .B(B), .C(C), .D(D), .e(seg_e));
  segmento_f segmento_f_1 (.A(A), .B(B), .C(C), .D(D), .f(seg_f));
  segmento_g segmento_g_1 (.A(A), .B(B), .C(C), .D(D), .g(seg_g));
endmodule
