// Logisim project PracticaLOGISIM.circ as structural Verilog: 17 circuits, main circuit MAINALU
module MAINALU (
  input  S2,
  input  S1,
  input  S0,
  input  in_4,
  input  [7:0] A,
  input  [7:0] B,
  output [7:0] out_7
);

  wire [7:0] and8bits_1_s, multiplicador8bits_1_s, not8bits_1_s, or8bits_1_s, restador8bits_1_s,
       sumador8bits_1_s, xnor8bits_1_s, xor8bits_1_s;

  MULTIPLICADOR8Bits multiplicador8bits_1 (.A(A), .Bmsign(B), .S(multiplicador8bits_1_s));
  RESTADOR8Bits restador8bits_1 (.CIN(in_4), .A(A), .B(B), .S(restador8bits_1_s));
  SUMADOR8Bits sumador8bits_1 (.A(A), .B(B), .S(sumador8bits_1_s));  // open: CIN
  XNOR8Bits xnor8bits_1 (.A(A), .B(B), .S(xnor8bits_1_s));
  XOR8Bits xor8bits_1 (.A(A), .B(B), .S(xor8bits_1_s));
  OR8Bits or8bits_1 (.A(A), .B(B), .S(or8bits_1_s));
  AND8Bits and8bits_1 (.A(A), .B(B), .S(and8bits_1_s));
  NOT8Bits not8bits_1 (.A(A), .S(not8bits_1_s));
  MULTIPLEXOR8Bitsa1Bit multiplexor8bitsa1bit_1 (
    .S2(S2), .S1(S1), .S0(S0), .I7multiplicador(multiplicador8bits_1_s), .I6restador(restador8bits_1_s),
    .I5sumador(sumador8bits_1_s), .I4xnor(xnor8bits_1_s), .I3xor(xor8bits_1_s), .I2or(or8bits_1_s),
    .I1and(and8bits_1_s), .I0not(not8bits_1_s), .S(out_7));
endmodule

module MULTIPLEXOR8Bitsa1Bit (
  input  S2,
  input  S1,
  input  S0,
  input  [7:0] I7multiplicador,
  input  [7:0] I6restador,
  input  [7:0] I5sumador,
  input  [7:0] I4xnor,
  input  [7:0] I3xor,
  input  [7:0] I2or,
  input  [7:0] I1and,
  input  [7:0] I0not,
  output [7:0] S
);

  MULTIPLEXOR multiplexor_1 (
    .S2(S2), .S1(S1), .S0(S0), .I0(I0not[0]), .I1(I1and[0]), .I2(I2or[0]), .I3(I3xor[0]), .I4(I4xnor[0]),
    .I5(I5sumador[0]), .I6(I6restador[0]), .I7(I7multiplicador[0]), .Y(S[0]));
  MULTIPLEXOR multiplexor_2 (
    .S2(S2), .S1(S1), .S0(S0), .I0(I0not[1]), .I1(I1and[1]), .I2(I2or[1]), .I3(I3xor[1]), .I4(I4xnor[1]),
    .I5(I5sumador[1]), .I6(I6restador[1]), .I7(I7multiplicador[1]), .Y(S[1]));
  MULTIPLEXOR multiplexor_3 (
    .S2(S2), .S1(S1), .S0(S0), .I0(I0not[2]), .I1(I1and[2]), .I2(I2or[2]), .I3(I3xor[2]), .I4(I4xnor[2]),
    .I5(I5sumador[2]), .I6(I6restador[2]), .I7(I7multiplicador[2]), .Y(S[2]));
  MULTIPLEXOR multiplexor_4 (
    .S2(S2), .S1(S1), .S0(S0), .I0(I0not[3]), .I1(I1and[3]), .I2(I2or[3]), .I3(I3xor[3]), .I4(I4xnor[3]),
    .I5(I5sumador[3]), .I6(I6restador[3]), .I7(I7multiplicador[3]), .Y(S[3]));
  MULTIPLEXOR multiplexor_5 (
    .S2(S2), .S1(S1), .S0(S0), .I0(I0not[4]), .I1(I1and[4]), .I2(I2or[4]), .I3(I3xor[4]), .I4(I4xnor[4]),
    .I5(I5sumador[4]), .I6(I6restador[4]), .I7(I7multiplicador[4]), .Y(S[4]));
  MULTIPLEXOR multiplexor_6 (
    .S2(S2), .S1(S1), .S0(S0), .I0(I0not[5]), .I1(I1and[5]), .I2(I2or[5]), .I3(I3xor[5]), .I4(I4xnor[5]),
    .I5(I5sumador[5]), .I6(I6restador[5]), .I7(I7multiplicador[5]), .Y(S[5]));
  MULTIPLEXOR multiplexor_7 (
    .S2(S2), .S1(S1), .S0(S0), .I0(I0not[6]), .I1(I1and[6]), .I2(I2or[6]), .I3(I3xor[6]), .I4(I4xnor[6]),
    .I5(I5sumador[6]), .I6(I6restador[6]), .I7(I7multiplicador[6]), .Y(S[6]));
  MULTIPLEXOR multiplexor_8 (
    .S2(S2), .S1(S1), .S0(S0), .I0(I0not[7]), .I1(I1and[7]), .I2(I2or[7]), .I3(I3xor[7]), .I4(I4xnor[7]),
    .I5(I5sumador[7]), .I6(I6restador[7]), .I7(I7multiplicador[7]), .Y(S[7]));
endmodule

module MULTIPLEXOR (
  input  S2,
  input  S1,
  input  S0,
  input  I0,
  input  I1,
  input  I2,
  input  I3,
  input  I4,
  input  I5,
  input  I6,
  input  I7,
  output Y
);

  wire and_1_out, and_2_out, and_3_out, and_4_out, and_5_out, and_6_out, and_7_out, and_8_out, and_9_out,
       and_10_out, and_11_out, and_12_out, and_13_out, and_14_out, and_15_out, and_16_out, and_17_out,
       and_18_out, and_19_out, and_20_out, and_21_out, and_22_out, and_23_out, and_24_out, not_1_out,
       not_2_out, not_3_out, or_1_out, or_2_out, or_3_out, or_4_out, or_5_out, or_6_out;

  not not_1 (not_1_out, S2);
  not not_2 (not_2_out, S1);
  not not_3 (not_3_out, S0);
  and and_1 (and_1_out, not_1_out, not_2_out);
  and and_2 (and_2_out, not_3_out, I0);
  and and_3 (and_3_out, not_1_out, not_2_out);
  and and_4 (and_4_out, S0, I1);
  and and_5 (and_5_out, not_1_out, S1);
  and and_6 (and_6_out, not_3_out, I2);
  and and_7 (and_7_out, not_1_out, S1);
  and and_8 (and_8_out, S0, I3);
  and and_9 (and_9_out, S2, not_2_out);
  and and_10 (and_10_out, not_3_out, I4);
  and and_11 (and_11_out, S2, not_2_out);
  and and_12 (and_12_out, S0, I5);
  and and_13 (and_13_out, S2, S1);
  and and_14 (and_14_out, not_3_out, I6);
  and and_15 (and_15_out, S2, S1);
  and and_16 (and_16_out, S0, I7);
  and and_17 (and_17_out, and_1_out, and_2_out);
  or or_1 (or_1_out, and_17_out, and_18_out);
  and and_18 (and_18_out, and_3_out, and_4_out);
  and and_19 (and_19_out, and_5_out, and_6_out);
  or or_2 (or_2_out, and_19_out, and_20_out);
  and and_20 (and_20_out, and_7_out, and_8_out);
  and and_21 (and_21_out, and_9_out, and_10_out);
  or or_3 (or_3_out, and_21_out, and_22_out);
  and and_22 (and_22_out, and_11_out, and_12_out);
  and and_23 (and_23_out, and_13_out, and_14_out);
  or or_4 (or_4_out, and_23_out, and_24_out);
  and and_24 (and_24_out, and_15_out, and_16_out);
  or or_5 (or_5_out, or_1_out, or_2_out);
  or or_6 (or_6_out, or_3_out, or_4_out);
  or or_7 (Y, or_5_out, or_6_out);
endmodule

module NOT8Bits (
  input  [7:0] A,
  output [7:0] S
);

  not not_1 (S[3], A[3]);
  not not_2 (S[4], A[4]);
  not not_3 (S[0], A[0]);
  not not_4 (S[1], A[1]);
  not not_5 (S[2], A[2]);
  not not_6 (S[5], A[5]);
  not not_7 (S[6], A[6]);
  not not_8 (S[7], A[7]);
endmodule

module AND8Bits (
  input  [7:0] A,
  input  [7:0] B,
  output [7:0] S
);

  and and_1 (S[0], A[0], B[0]);
  and and_2 (S[1], A[1], B[1]);
  and and_3 (S[2], A[2], B[2]);
  and and_4 (S[3], A[3], B[3]);
  and and_5 (S[4], A[4], B[4]);
  and and_6 (S[5], A[5], B[5]);
  and and_7 (S[6], A[6], B[6]);
  and and_8 (S[7], A[7], B[7]);
endmodule

module OR8Bits (
  input  [7:0] A,
  input  [7:0] B,
  output [7:0] S
);

  or or_1 (S[0], A[0], B[0]);
  or or_2 (S[1], A[1], B[1]);
  or or_3 (S[2], A[2], B[2]);
  or or_4 (S[3], A[3], B[3]);
  or or_5 (S[4], A[4], B[4]);
  or or_6 (S[5], A[5], B[5]);
  or or_7 (S[6], A[6], B[6]);
  or or_8 (S[7], A[7], B[7]);
endmodule

module XOR8Bits (
  input  [7:0] A,
  input  [7:0] B,
  output [7:0] S
);

  xor xor_1 (S[0], A[0], B[0]);
  xor xor_2 (S[1], A[1], B[1]);
  xor xor_3 (S[2], A[2], B[2]);
  xor xor_4 (S[3], A[3], B[3]);
  xor xor_5 (S[4], A[4], B[4]);
  xor xor_6 (S[5], A[5], B[5]);
  xor xor_7 (S[6], A[6], B[6]);
  xor xor_8 (S[7], A[7], B[7]);
endmodule

module XNOR8Bits (
  input  [7:0] A,
  input  [7:0] B,
  output [7:0] S
);

  wire xor_1_out, xor_2_out, xor_3_out, xor_4_out, xor_5_out, xor_6_out, xor_7_out, xor_8_out;

  xor xor_1 (xor_1_out, A[0], B[0]);
  not not_1 (S[0], xor_1_out);
  xor xor_2 (xor_2_out, A[1], B[1]);
  not not_2 (S[1], xor_2_out);
  xor xor_3 (xor_3_out, A[2], B[2]);
  not not_3 (S[2], xor_3_out);
  xor xor_4 (xor_4_out, A[3], B[3]);
  not not_4 (S[3], xor_4_out);
  xor xor_5 (xor_5_out, A[4], B[4]);
  not not_5 (S[4], xor_5_out);
  xor xor_6 (xor_6_out, A[5], B[5]);
  not not_6 (S[5], xor_6_out);
  xor xor_7 (xor_7_out, A[6], B[6]);
  not not_7 (S[6], xor_7_out);
  xor xor_8 (xor_8_out, A[7], B[7]);
  not not_8 (S[7], xor_8_out);
endmodule

module SUMADOR8Bits (
  input  CIN,
  input  [7:0] A,
  input  [7:0] B,
  output [7:0] S
);

  wire sumador4bits_1_cout;

  SUMADOR4Bits sumador4bits_1 (
    .A0(A[0]), .B0(B[0]), .CIN(CIN), .A1(A[1]), .B1(B[1]), .A2(A[2]), .B2(B[2]), .A3(A[3]), .B3(B[3]),
    .S1(S[0]), .S2(S[1]), .S3(S[2]), .S4(S[3]), .COUT(sumador4bits_1_cout));
  SUMADOR4Bits sumador4bits_2 (
    .A0(A[4]), .B0(B[4]), .CIN(sumador4bits_1_cout), .A1(A[5]), .B1(B[5]), .A2(A[6]), .B2(B[6]), .A3(A[7]),
    .B3(B[7]), .S1(S[4]), .S2(S[5]), .S3(S[6]), .S4(S[7]));  // open: COUT
endmodule

module RESTADOR8Bits (
  input  CIN,
  input  [7:0] A,
  input  [7:0] B,
  output [7:0] S
);

  wire [7:0] not_1_out;

  assign not_1_out = ~B;  // NOT_Gate not_1, 8 bits wide
  SUMADOR8Bits sumador8bits_1 (.CIN(CIN), .A(A), .B(not_1_out), .S(S));
endmodule

module SUMADOR4Bits (
  input  A0,
  input  B0,
  input  CIN,
  input  A1,
  input  B1,
  input  A2,
  input  B2,
  input  A3,
  input  B3,
  output S1,
  output S2,
  output S3,
  output S4,
  output COUT
);

  wire sumador2bits_1_cout;

  SUMADOR2Bits sumador2bits_1 (
    .A0(A0), .B0(B0), .CIN(CIN), .A1(A1), .B1(B1), .S1(S1), .S2(S2), .COUT(sumador2bits_1_cout));
  SUMADOR2Bits sumador2bits_2 (
    .A0(A2), .B0(B2), .CIN(sumador2bits_1_cout), .A1(A3), .B1(B3), .S1(S3), .S2(S4), .COUT(COUT));
endmodule

module SUMADOR2Bits (
  input  A0,
  input  B0,
  input  CIN,
  input  A1,
  input  B1,
  output S1,
  output S2,
  output COUT
);

  wire sumador1bit_1_cout;

  SUMADOR1Bit sumador1bit_1 (.A(A0), .B(B0), .CIN(CIN), .S(S1), .COUT(sumador1bit_1_cout));
  SUMADOR1Bit sumador1bit_2 (.A(A1), .B(B1), .CIN(sumador1bit_1_cout), .S(S2), .COUT(COUT));
endmodule

module SUMADOR1Bit (
  input  A,
  input  B,
  input  CIN,
  output S,
  output COUT
);

  wire and_1_out, and_2_out, and_3_out, and_4_out, and_5_out, and_6_out, and_7_out, and_8_out, and_9_out,
       and_10_out, and_11_out, not_1_out, not_2_out, not_3_out, or_1_out, or_2_out, or_4_out;

  not not_1 (not_1_out, A);
  not not_2 (not_2_out, B);
  not not_3 (not_3_out, CIN);
  and and_1 (and_1_out, not_1_out, not_2_out);
  and and_2 (and_2_out, not_1_out, B);
  and and_3 (and_3_out, A, not_2_out);
  and and_4 (and_4_out, A, B);
  and and_5 (and_5_out, B, CIN);
  and and_6 (and_6_out, A, CIN);
  and and_7 (and_7_out, and_1_out, CIN);
  and and_8 (and_8_out, and_2_out, not_3_out);
  and and_9 (and_9_out, and_3_out, not_3_out);
  and and_10 (and_10_out, and_4_out, CIN);
  or or_1 (or_1_out, and_5_out, and_6_out);
  and and_11 (and_11_out, A, B);
  or or_2 (or_2_out, and_7_out, and_8_out);
  or or_3 (S, or_2_out, or_4_out);
  or or_4 (or_4_out, and_9_out, and_10_out);
  or or_5 (COUT, or_1_out, and_11_out);
endmodule

module MULTIPLICADOR8Bits (
  input  [7:0] A,
  input  [7:0] Bmsign,
  output [7:0] S
);

  wire [7:0] multiplicador1bit_1_s, multiplicador1bit_2_s, multiplicador1bit_3_s, multiplicador1bit_4_s,
       multiplicador1bit_5_s, multiplicador1bit_6_s, multiplicador1bit_7_s, multiplicador1bit_8_s,
       shiftmultiplicador1bit_1_s, shiftmultiplicador1bit_2_s, shiftmultiplicador1bit_3_s,
       shiftmultiplicador1bit_4_s, shiftmultiplicador2bits_1_s, shiftmultiplicador2bits_2_s,
       shiftmultiplicador2bits_3_s, shiftmultiplicador2bits_4_s, shiftmultiplicador2bits_5_s,
       shiftmultiplicador2bits_6_s, shiftmultiplicador2bits_7_s, shiftmultiplicador2bits_8_s,
       shiftmultiplicador2bits_9_s, shiftmultiplicador2bits_10_s, shiftmultiplicador2bits_11_s,
       shiftmultiplicador2bits_12_s, sumador8bits_1_s, sumador8bits_2_s, sumador8bits_3_s, sumador8bits_4_s,
       sumador8bits_5_s, sumador8bits_6_s;

  MULTIPLICADOR1Bit multiplicador1bit_1 (.A(A), .B(Bmsign[0]), .S(multiplicador1bit_1_s));
  MULTIPLICADOR1Bit multiplicador1bit_2 (.A(A), .B(Bmsign[1]), .S(multiplicador1bit_2_s));
  MULTIPLICADOR1Bit multiplicador1bit_3 (.A(A), .B(Bmsign[2]), .S(multiplicador1bit_3_s));
  MULTIPLICADOR1Bit multiplicador1bit_4 (.A(A), .B(Bmsign[3]), .S(multiplicador1bit_4_s));
  MULTIPLICADOR1Bit multiplicador1bit_5 (.A(A), .B(Bmsign[4]), .S(multiplicador1bit_5_s));
  MULTIPLICADOR1Bit multiplicador1bit_6 (.A(A), .B(Bmsign[5]), .S(multiplicador1bit_6_s));
  MULTIPLICADOR1Bit multiplicador1bit_7 (.A(A), .B(Bmsign[6]), .S(multiplicador1bit_7_s));
  MULTIPLICADOR1Bit multiplicador1bit_8 (.A(A), .B(Bmsign[7]), .S(multiplicador1bit_8_s));
  SHIFTMULTIPLICADOR1Bit shiftmultiplicador1bit_1 (.A(multiplicador1bit_2_s), .S(shiftmultiplicador1bit_1_s));
  SHIFTMULTIPLICADOR2Bits shiftmultiplicador2bits_1 (.A(multiplicador1bit_3_s), .S(shiftmultiplicador2bits_1_s));
  SHIFTMULTIPLICADOR2Bits shiftmultiplicador2bits_2 (.A(multiplicador1bit_4_s), .S(shiftmultiplicador2bits_2_s));
  SHIFTMULTIPLICADOR2Bits shiftmultiplicador2bits_3 (.A(multiplicador1bit_5_s), .S(shiftmultiplicador2bits_3_s));
  SHIFTMULTIPLICADOR2Bits shiftmultiplicador2bits_4 (.A(multiplicador1bit_6_s), .S(shiftmultiplicador2bits_4_s));
  SHIFTMULTIPLICADOR2Bits shiftmultiplicador2bits_5 (.A(multiplicador1bit_7_s), .S(shiftmultiplicador2bits_5_s));
  SHIFTMULTIPLICADOR2Bits shiftmultiplicador2bits_6 (.A(multiplicador1bit_8_s), .S(shiftmultiplicador2bits_6_s));
  SUMADOR8Bits sumador8bits_1 (
    .A(multiplicador1bit_1_s), .B(shiftmultiplicador1bit_1_s), .S(sumador8bits_1_s));  // open: CIN
  SHIFTMULTIPLICADOR1Bit shiftmultiplicador1bit_2 (.A(shiftmultiplicador2bits_2_s), .S(shiftmultiplicador1bit_2_s));
  SHIFTMULTIPLICADOR2Bits shiftmultiplicador2bits_7 (.A(shiftmultiplicador2bits_3_s), .S(shiftmultiplicador2bits_7_s));
  SHIFTMULTIPLICADOR2Bits shiftmultiplicador2bits_8 (.A(shiftmultiplicador2bits_4_s), .S(shiftmultiplicador2bits_8_s));
  SHIFTMULTIPLICADOR2Bits shiftmultiplicador2bits_9 (.A(shiftmultiplicador2bits_5_s), .S(shiftmultiplicador2bits_9_s));
  SHIFTMULTIPLICADOR2Bits shiftmultiplicador2bits_10 (
    .A(shiftmultiplicador2bits_6_s), .S(shiftmultiplicador2bits_10_s));
  SUMADOR8Bits sumador8bits_2 (
    .A(sumador8bits_1_s), .B(shiftmultiplicador2bits_1_s), .S(sumador8bits_2_s));  // open: CIN
  SHIFTMULTIPLICADOR1Bit shiftmultiplicador1bit_3 (.A(shiftmultiplicador2bits_8_s), .S(shiftmultiplicador1bit_3_s));
  SHIFTMULTIPLICADOR2Bits shiftmultiplicador2bits_11 (
    .A(shiftmultiplicador2bits_9_s), .S(shiftmultiplicador2bits_11_s));
  SHIFTMULTIPLICADOR2Bits shiftmultiplicador2bits_12 (
    .A(shiftmultiplicador2bits_10_s), .S(shiftmultiplicador2bits_12_s));
  SHIFTMULTIPLICADOR1Bit shiftmultiplicador1bit_4 (.A(shiftmultiplicador2bits_12_s), .S(shiftmultiplicador1bit_4_s));
  SUMADOR8Bits sumador8bits_3 (
    .A(sumador8bits_2_s), .B(shiftmultiplicador1bit_2_s), .S(sumador8bits_3_s));  // open: CIN
  SUMADOR8Bits sumador8bits_4 (
    .A(sumador8bits_3_s), .B(shiftmultiplicador2bits_7_s), .S(sumador8bits_4_s));  // open: CIN
  SUMADOR8Bits sumador8bits_5 (
    .A(sumador8bits_4_s), .B(shiftmultiplicador1bit_3_s), .S(sumador8bits_5_s));  // open: CIN
  SUMADOR8Bits sumador8bits_6 (
    .A(sumador8bits_5_s), .B(shiftmultiplicador2bits_11_s), .S(sumador8bits_6_s));  // open: CIN
  SUMADOR8Bits sumador8bits_7 (.A(sumador8bits_6_s), .B(shiftmultiplicador1bit_4_s), .S(S));  // open: CIN
endmodule

module MULTIPLICADOR1Bit (
  input  [7:0] A,
  input  B,
  output [7:0] S
);

  AND8Bits and8bits_1 (.A(A), .B({8{B}}), .S(S));
endmodule

module SHIFTMULTIPLICADOR1Bit (
  input  [7:0] A,
  output [7:0] S
);


  assign S = {A[6:0], 1'b0};
endmodule

module SHIFTMULTIPLICADOR2Bits (
  input  [7:0] A,
  output [7:0] S
);


  assign S = {A[5:0], 2'b00};
endmodule
