// Logisim project sumador.circ as structural Verilog: 4 circuits, main circuit sumadorUno
module sumadorUno (
  input  A,
  input  B,
  input  Cin,
  output Fo,
  output Cout
);

  wire and_1_out, and_2_out, and_3_out, and_4_out, and_5_out, and_6_out, and_7_out, and_8_out, and_9_out,
       and_10_out, and_11_out, not_1_out, not_2_out, not_3_out, or_1_out, or_2_out, or_4_out;

  not not_1 (not_1_out, A);
  not not_2 (not_2_out, B);
  not not_3 (not_3_out, Cin);
  and and_1 (and_1_out, not_1_out, not_2_out);
  and and_2 (and_2_out, not_1_out, B);
  and and_3 (and_3_out, A, not_2_out);
  and and_4 (and_4_out, A, B);
  and and_5 (and_5_out, B, Cin);
  and and_6 (and_6_out, A, Cin);
  and and_7 (and_7_out, and_1_out, Cin);
  and and_8 (and_8_out, and_2_out, not_3_out);
  and and_9 (and_9_out, and_3_out, not_3_out);
  and and_10 (and_10_out, and_4_out, Cin);
  or or_1 (or_1_out, and_5_out, and_6_out);
  and and_11 (and_11_out, A, B);
  or or_2 (or_2_out, and_7_out, and_8_out);
  or or_3 (Fo, or_2_out, or_4_out);
  or or_4 (or_4_out, and_9_out, and_10_out);
  or or_5 (Cout, or_1_out, and_11_out);
endmodule

module sumadorDos (
  input  X1,
  input  X2,
  input  Y1,
  input  Y2,
  input  Cin,
  output Uno,
  output Dos,
  output Cout
);

  wire sumadoruno_1_cout;

  sumadorUno sumadoruno_1 (.A(X2), .B(Y2), .Cin(Cin), .Fo(Uno), .Cout(sumadoruno_1_cout));
  sumadorUno sumadoruno_2 (.A(X1), .B(Y1), .Cin(sumadoruno_1_cout), .Fo(Dos), .Cout(Cout));
endmodule

module sumadorCuatro (
  input  X1,
  input  X2,
  input  X3,
  input  X4,
  input  Y1,
  input  Y2,
  input  Y3,
  input  Y4,
  input  Cin,
  output Uno,
  output Dos,
  output Tres,
  output Cuatro,
  output Cout
);

  wire sumadordos_1_cout;

  sumadorDos sumadordos_1 (
    .X1(X3), .X2(X4), .Y1(Y3), .Y2(Y4), .Cin(Cin), .Uno(Uno), .Dos(Dos), .Cout(sumadordos_1_cout));
  sumadorDos sumadordos_2 (
    .X1(X1), .X2(X2), .Y1(Y1), .Y2(Y2), .Cin(sumadordos_1_cout), .Uno(Tres), .Dos(Cuatro), .Cout(Cout));
endmodule

module sumadorOcho (
  input  X1,
  input  X2,
  input  X3,
  input  X4,
  input  X5,
  input  X6,
  input  X7,
  input  X8,
  input  Y1,
  input  Y2,
  input  Y3,
  input  Y4,
  input  Y5,
  input  Y6,
  input  Y7,
  input  Y8,
  input  Cin,
  output out_18,
  output out_19,
  output out_20,
  output out_21,
  output out_22,
  output out_23,
  output out_24,
  output out_25,
  output Cout
);

  wire sumadorcuatro_1_cout;

  sumadorCuatro sumadorcuatro_1 (
    .X1(X5), .X2(X6), .X3(X7), .X4(X8), .Y1(Y5), .Y2(Y6), .Y3(Y7), .Y4(Y8), .Cin(Cin), .Uno(out_18),
    .Dos(out_19), .Tres(out_20), .Cuatro(out_21), .Cout(sumadorcuatro_1_cout));
  sumadorCuatro sumadorcuatro_2 (
    .X1(X1), .X2(X2), .X3(X3), .X4(X4), .Y1(Y1), .Y2(Y2), .Y3(Y3), .Y4(Y4), .Cin(sumadorcuatro_1_cout),
    .Uno(out_22), .Dos(out_23), .Tres(out_24), .Cuatro(out_25), .Cout(Cout));
endmodule
